# Fritzing sketch electrical_ckt (saved by Fritzing 0.9.3b)
breadboards: 1

parts:
  U1 = ESP32S-HiLetgo [part_number=ESP32S-HiLetgo]
  M1 = DC Motor
  R1 = Resistor [tolerance=±5% resistance=220 package="0402 [SMD]"]
  U3 = RELAY [package=relay-jzc]
  BAT1 = BC9VPC [package=bc9vpc]
  RHT1 = Humidity and Temperature Sensor RHT03
  WeMos_D1_Mini_Relay_Shield_V1 = WeMos D1 Mini Relay Shield V2
  U4 = RELAY [package=relay-jzc]
  U5 = RELAY [package=relay-jzc]

nets:
  VCC: U1.3.3, U3.NO, RHT1.Vcc, WeMos_D1_Mini_Relay_Shield_V1.3V3, U4.NO, U5.NO
  N1: U1.GPIO34, U3.COIL2
  N2: U1.GPIO12, WeMos_D1_Mini_Relay_Shield_V1.D7
  N3: U1.GND, RHT1.GND_1, WeMos_D1_Mini_Relay_Shield_V1.G
  N4: U1.GPIO9, RHT1.Data-signal
  N5: U1.GPIO22, U4.COIL2
  N6: U1.GPIO23, U5.COIL2
  N7: M1.pin_1, R1.Pin_0, BAT1.V-
  N8: M1.pin_2, R1.Pin_1, WeMos_D1_Mini_Relay_Shield_V1.NO
  N9: BAT1.V+, WeMos_D1_Mini_Relay_Shield_V1.COM

custom parts:
  ESP32S-HiLetgo: HiLetgo ESP-WROOM-32 ESP32 ESP-32S Development Board 2.4GHz Dual-Mode WiFi + Bluetooth Dual Cores Microcontroller The ESP32 integrated with Antenna switches, RF Balun, power amplifiers, low-noise amplifiers, filters, and management modules, and the entire solution occupies the least area of PCB. 2.4 GHz Wi-Fi plus Bluetooth dual-mode chip, with TSMC Ultra-low power consumption 40nm technology,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
